// Logisim project 5exe1.circ as structural Verilog: 1 circuit, main circuit main
module main (
  input  x3,
  input  x2,
  input  x1,
  input  x0,
  output out_5
);

  wire and_1_out, and_2_out, and_3_out, and_4_out, not_1_out, not_2_out;

  not not_1 (not_1_out, x3);
  not not_2 (not_2_out, x2);
  and and_1 (and_1_out, not_1_out, not_2_out);
  and and_2 (and_2_out, x3, x2);
  and and_3 (and_3_out, x3, x0);
  and and_4 (and_4_out, x3, x1);
  or or_1 (out_5, and_1_out, and_2_out, and_3_out, and_4_out);
endmodule
