// Logisim project 4x1multi.circ as structural Verilog: 1 circuit, main circuit main
module main (
  input  A,
  input  S1,
  input  B,
  input  S3,
  input  C,
  input  S2,
  input  D,
  output Y
);

  wire and_1_out, and_2_out, and_3_out, and_4_out, and_5_out, and_6_out, not_1_out, not_2_out, not_3_out,
       or_1_out, or_2_out;

  not not_1 (not_1_out, S1);
  not not_2 (not_2_out, S2);
  and and_1 (and_1_out, A, S1);
  and and_2 (and_2_out, not_1_out, B);
  and and_3 (and_3_out, C, S2);
  and and_4 (and_4_out, not_2_out, D);
  or or_1 (or_1_out, and_1_out, and_2_out);
  or or_2 (or_2_out, and_3_out, and_4_out);
  not not_3 (not_3_out, S3);
  and and_5 (and_5_out, or_1_out, S3);
  and and_6 (and_6_out, not_3_out, or_2_out);
  or or_3 (Y, and_5_out, and_6_out);
endmodule
