// Logisim project 4bit.circ as structural Verilog: 4 circuits, main circuit onebit
module onebit (
  input  A,
  input  B,
  input  Cin,
  output S,
  output Cout
);

  wire and_1_out, and_2_out, xor_1_out;

  xor xor_1 (xor_1_out, A, B);
  xor xor_2 (S, xor_1_out, Cin);
  and and_1 (and_1_out, xor_1_out, Cin);
  and and_2 (and_2_out, A, B);
  or or_1 (Cout, and_1_out, and_2_out);
endmodule

module fourbit (
  input  [3:0] A,
  input  [3:0] B,
  input  Cin,
  output [3:0] S,
  output Cout
);

  wire onebit_1_cout, onebit_2_cout, onebit_3_cout;

  onebit onebit_1 (.A(A[0]), .B(B[0]), .Cin(Cin), .S(S[0]), .Cout(onebit_1_cout));
  onebit onebit_2 (.A(A[1]), .B(B[1]), .Cin(onebit_1_cout), .S(S[1]), .Cout(onebit_2_cout));
  onebit onebit_3 (.A(A[2]), .B(B[2]), .Cin(onebit_2_cout), .S(S[2]), .Cout(onebit_3_cout));
  onebit onebit_4 (.A(A[3]), .B(B[3]), .Cin(onebit_3_cout), .S(S[3]), .Cout(Cout));
endmodule

module sixteenbit (
  input  [15:0] A,
  input  [15:0] B,
  input  Cin,
  output [15:0] S,
  output Cout
);

  wire fourbit_1_cout, fourbit_2_cout, fourbit_3_cout;

  fourbit fourbit_1 (.A(A[3:0]), .B(B[3:0]), .Cin(Cin), .S(S[3:0]), .Cout(fourbit_1_cout));
  fourbit fourbit_2 (.A(A[7:4]), .B(B[7:4]), .Cin(fourbit_1_cout), .S(S[7:4]), .Cout(fourbit_2_cout));
  fourbit fourbit_3 (.A(A[11:8]), .B(B[11:8]), .Cin(fourbit_2_cout), .S(S[11:8]), .Cout(fourbit_3_cout));
  fourbit fourbit_4 (.A(A[15:12]), .B(B[15:12]), .Cin(fourbit_3_cout), .S(S[15:12]), .Cout(Cout));
endmodule

module thirtytwobit (
  input  [31:0] A,
  input  [31:0] B,
  input  Cin,
  output Cout,
  output [31:0] S
);

  wire sixteenbit_1_cout;

  sixteenbit sixteenbit_1 (.A(A[15:0]), .B(B[15:0]), .Cin(Cin), .S(S[15:0]), .Cout(sixteenbit_1_cout));
  sixteenbit sixteenbit_2 (.A(A[31:16]), .B(B[31:16]), .Cin(sixteenbit_1_cout), .S(S[31:16]), .Cout(Cout));
endmodule
