// Logisim project First_FSMe.circ as structural Verilog: 4 circuits, main circuit FSM
module FSM (
  input  FSM_Input,
  output Out1
);

  wire clock_1_out;
  wire [1:0] fsmlogic_1_next_state, register_1_q;

  Clock clock_1 (.out(clock_1_out));
  Register #(.width(2)) register_1 (.D(fsmlogic_1_next_state), .clk(clock_1_out), .Q(register_1_q));  // open: en, clr
  FSMLogic fsmlogic_1 (
    .Input_Bit(FSM_Input), .Current_State(register_1_q), .Output1(Out1), .Next_State(fsmlogic_1_next_state));
endmodule

module FSMLogic (
  input  Input_Bit,
  input  [1:0] Current_State,
  output Output1,
  output [1:0] Next_State
);

  wire and_1_out, and_2_out, not_1_out, not_2_out, not_3_out;

  not not_1 (not_1_out, Current_State[1]);
  not not_2 (not_2_out, Current_State[0]);
  not not_3 (not_3_out, Input_Bit);
  and and_1 (and_1_out, Input_Bit, not_1_out);
  and and_2 (and_2_out, not_3_out, not_2_out);
  or or_1 (Output1, and_1_out, and_2_out);
  StateBitZero statebitzero_1 (
    .In1(Input_Bit), .State_Bit_0(Current_State[0]), .State_Bit_1(Current_State[1]),
    .New_State_0(Next_State[0]));
  StateBitOne statebitone_1 (
    .In1(Input_Bit), .State_Bit_0(Current_State[0]), .State_Bit_1(Current_State[1]),
    .New_State_1(Next_State[1]));
endmodule

module StateBitOne (
  input  In1,
  input  State_Bit_0,
  input  State_Bit_1,
  output New_State_1
);

  wire not_1_out, not_2_out, not_3_out;

  not not_1 (not_1_out, In1);
  not not_2 (not_2_out, State_Bit_0);
  not not_3 (not_3_out, State_Bit_1);
  or or_1 (New_State_1, In1, State_Bit_0);
endmodule

module StateBitZero (
  input  In1,
  input  State_Bit_0,
  input  State_Bit_1,
  output New_State_0
);

  wire not_1_out, not_2_out, not_3_out;

  not not_1 (not_1_out, In1);
  not not_2 (not_2_out, State_Bit_0);
  not not_3 (not_3_out, State_Bit_1);
  or or_1 (New_State_0, not_1_out, State_Bit_1);
endmodule
