// Logisim project 8.circ as structural Verilog: 1 circuit, main circuit main
module main (
  input  [3:0] Input1,
  input  [3:0] Input2,
  input  in_3,
  output [3:0] Output1,
  output out_5
);

  wire [3:0] adder_1_out, multiplexer_1_out, not_1_out;

  // Probe on not_1_out
  assign not_1_out = ~Input2;  // NOT_Gate not_1, 4 bits wide
  // Probe on adder_1_out
  Adder #(.width(4)) adder_1 (.a(not_1_out), .b(4'b0001), .out(adder_1_out));  // open: cin, cout
  Multiplexer #(.width(4), .enable("false")) multiplexer_1 (
    .in0(Input2), .in1(adder_1_out), .out(multiplexer_1_out), .sel(in_3));
  Adder #(.width(4)) adder_2 (.a(Input1), .b(multiplexer_1_out), .out(Output1), .cout(out_5));  // open: cin
endmodule
