// Logisim project sequence_detector.circ as structural Verilog: 2 circuits, main circuit main
module main (
  input  Cs1,
  input  Cs0,
  input  Cin,
  output Ns1,
  output Ns0,
  output Cout
);

  wire and_1_out, and_2_out, and_3_out, and_4_out, and_5_out, and_6_out, and_7_out, not_1_out, not_2_out,
       not_3_out, not_4_out, not_5_out, not_6_out, not_7_out;

  not not_1 (not_1_out, Cs0);
  not not_2 (not_2_out, Cs1);
  not not_3 (not_3_out, Cs0);
  not not_4 (not_4_out, Cs0);
  not not_5 (not_5_out, Cin);
  not not_6 (not_6_out, Cin);
  not not_7 (not_7_out, Cin);
  and and_1 (and_1_out, Cs0, Cin);
  and and_2 (and_2_out, Cs1, not_1_out);
  and and_3 (and_3_out, not_2_out, not_3_out, Cin);
  and and_4 (and_4_out, Cs1, not_4_out, not_5_out);
  and and_5 (and_5_out, Cs1, Cs0, Cin);
  and and_6 (and_6_out, Cs0, not_6_out);
  and and_7 (and_7_out, Cs1, not_7_out);
  or or_1 (Ns1, and_1_out, and_2_out);
  or or_2 (Ns0, and_3_out, and_4_out, and_5_out);
  or or_3 (Cout, and_6_out, and_7_out);
endmodule

module FinalCir (
  input  Cinput,
  output Cout
);

  wire clock_1_out;
  wire [1:0] main_1_ns1, register_1_q;

  Register #(.width(2)) register_1 (.D(main_1_ns1), .clk(clock_1_out), .Q(register_1_q));  // open: en, clr
  Clock clock_1 (.out(clock_1_out));
  main main_1 (
    .Cs1(register_1_q[0]), .Cs0(register_1_q[1]), .Cin(Cinput), .Ns1(main_1_ns1[0]), .Ns0(main_1_ns1[1]),
    .Cout(Cout));
endmodule
