// Logisim project SC_RISCV_1.circ as structural Verilog: 1 circuit, main circuit main
module main (
  input  in_1
);

  wire clock_1_out, not_1_out, registerfile_1_p1, registerfile_1_p7;
  wire [4:0] alu_1_p4, risc_vprogramrom_1_p2_3, risc_vprogramrom_1_p2_4;
  wire [7:0] rom_1_data;
  wire [14:0] risc_vprogramrom_1_p2_2;
  wire [31:0] adder_1_out, bitselector_1_out, multiplexer_1_out, register_1_q, registerfile_1_p8;
  wire [31:5] risc_vprogramrom_1_p2;

  Clock clock_1 (.out(clock_1_out));
  Register #(.width(32)) register_1 (.D(adder_1_out), .clk(clock_1_out), .Q(register_1_q), .clr(in_1));  // open: en
  Adder #(.width(32)) adder_1 (.a(32'h4), .b(register_1_q), .out(adder_1_out));  // open: cin, cout
  // Probe on {risc_vprogramrom_1_p2[31], risc_vprogramrom_1_p2[10:5], risc_vprogramrom_1_p2_4, risc_vprogramrom_1_p2_3, risc_vprogramrom_1_p2_2}
  // RISC_VProgramROM risc_vprogramrom_1: pin names not known; wires that end beside it: register_1_q, {risc_vprogramrom_1_p2[31], risc_vprogramrom_1_p2[10:5], risc_vprogramrom_1_p2_4, risc_vprogramrom_1_p2_3, risc_vprogramrom_1_p2_2}
  BitSelector #(.width(32), .group(32)) bitselector_1 (
    .in({{21{risc_vprogramrom_1_p2[31]}}, risc_vprogramrom_1_p2[10:5], risc_vprogramrom_1_p2_4}),
    .out(bitselector_1_out), .sel(not_1_out));
  not not_1 (not_1_out, rom_1_data[6]);
  // Probe on risc_vprogramrom_1_p2_2[14:12]
  // Probe on risc_vprogramrom_1_p2_2[6:2]
  ROM #(.addrWidth(9)) rom_1 (
    .addr({risc_vprogramrom_1_p2[10], risc_vprogramrom_1_p2_2[14:12], risc_vprogramrom_1_p2_2[6:2]}),
    .data(rom_1_data));
  // Probe on {risc_vprogramrom_1_p2[10], risc_vprogramrom_1_p2_2[14:12], risc_vprogramrom_1_p2_2[6:2]}
  // RegisterFile registerfile_1: pin names not known; wires that end beside it: registerfile_1_p1, clock_1_out, rom_1_data[5], risc_vprogramrom_1_p2_2[11:7], risc_vprogramrom_1_p2_3, risc_vprogramrom_1_p2_4, registerfile_1_p7, registerfile_1_p8
  // Probe on risc_vprogramrom_1_p2_4
  // Probe on risc_vprogramrom_1_p2_3
  Multiplexer #(.width(32), .enable("false")) multiplexer_1 (
    .in0(registerfile_1_p8), .in1(bitselector_1_out), .out(multiplexer_1_out), .sel(rom_1_data[4]));
  // Probe on rom_1_data[5]
  // ALU alu_1: pin names not known; wires that end beside it: registerfile_1_p7, multiplexer_1_out, rom_1_data[3:0], alu_1_p4, registerfile_1_p1
  Multiplexer #(.width(5), .enable("false")) multiplexer_2 (
    .in0(multiplexer_1_out[4:0]), .in1(risc_vprogramrom_1_p2_4), .out(alu_1_p4), .sel(rom_1_data[4]));
  // Probe on rom_1_data[3:0]

  // Notes on the sheet:
  //   Instruction Memory
  //   contents of risc_vprogramrom_1 (hex, n*v repeats v):
  //   addi x2, x0, 44 and x3, x1, x2
  //   contents of rom_1 (hex, n*v repeats v):
  //   4*0 7f 231*0 20 23*0 7f
endmodule
